# Fritzing sketch electric_circuit_diagramm (saved by Fritzing 0.9.4)
breadboards: 1

parts:
  WeMos_D1_Mini1 = WeMos D1 Mini
  HC-SR04_Sensor_1 = HC-SR04 Ultrasonic Distance Sensor

nets:
  5V: WeMos_D1_Mini1.5V, HC-SR04_Sensor_1.VCC
  N1: WeMos_D1_Mini1.D2, HC-SR04_Sensor_1.ECHO
  N2: WeMos_D1_Mini1.G, HC-SR04_Sensor_1.GND
